# Fritzing sketch DC_motor_control (saved by Fritzing 0.8.7b)
breadboards: 2

parts:
  Arduino2 = Arduino Uno (Rev3)
  IC2 = L293D [package=THT]
  M2 = DC Motor
  M3 = DC Motor
  IC3 = L293D [package=THT]
  M4 = DC Motor
  M5 = DC Motor
  U1 = 74HC595 [package="DIP16 [THT]"]

nets:
  N1: Arduino2.D10_PWM/SS, IC2.Enable_2
  N2: Arduino2.D11_PWM/MOSI, IC2.Enable_1
  N3: Arduino2.GND, IC2.0V, IC3.0V
  N4: Arduino2.D5_PWM, IC3.Enable_1
  N5: Arduino2.D6_PWM, IC3.Enable_2
  N6: Arduino2.5V, IC2.+Vmotor, IC2.+V, IC3.+Vmotor, IC3.+V
  N7: M2.pin_1, U1.Q4
  N8: M2.pin_2, U1.Q3
  N9: M3.pin_1, U1.Q0
  N10: M3.pin_2, U1.Q7
  N11: M4.pin_1, U1.Q2
  N12: M4.pin_2, U1.Q1
  N13: M5.pin_1, U1.Q6
  N14: M5.pin_2, U1.Q5

notes:
  This project shows how to control a DC motor's direction (running forwards and backwards) using an H-bridge. An H-bridge is an electronic circuit which enables a voltage to be applied across a load in either direction.
  http://itp.nyu.edu/physcomp/Labs/DCMotorControl
