# Fritzing sketch DC_motor_control2 (saved by Fritzing 0.9.1b)
breadboards: 1

parts:
  Arduino1 = Arduino Uno (Rev3)  # not connected
  IC2 = L293D [package=THT]
  M2 = DC Motor
  M3 = DC Motor
  M4 = DC Motor
  M5 = DC Motor

nets:
  N1: IC2.Enable_1, M4.pin_2
  N2: IC2.Out_1_(_Controlled_by_Enable_1_), M4.pin_1
  N3: IC2.Out_2_(_Controlled_by_Enable_1_), M2.pin_2
  N4: IC2.In_2, M2.pin_1
  N5: IC2.In_3, M5.pin_2
  N6: IC2.Out_3_(_Controlled_by_Enable_2_), M5.pin_1
  N7: IC2.Out_4_(_Controlled_by_Enable_2_), M3.pin_2
  N8: IC2.In_4, M3.pin_1

notes:
  This project shows how to control a DC motor's direction (running forwards and backwards) using an H-bridge. An H-bridge is an electronic circuit which enables a voltage to be applied across a load in either direction.
  http://itp.nyu.edu/physcomp/Labs/DCMotorControl
