# Fritzing sketch moving car (saved by Fritzing 0.9.1b)
circuit board: 6.88566cm x 5.36311cm
breadboards: 2

parts:
  Arduino2 = Arduino Uno (Rev3)
  IC1 = L293D [package=THT]
  M1 = DC Motor
  M4 = DC Motor
  IC2 = L293D [package=THT]
  M2 = DC Motor
  M3 = DC Motor
  U1 = 74HC595 [package="DIP16 [THT]"]

nets:
  N1: Arduino2.D8, U1.SH_CP
  N2: Arduino2.D9_PWM, IC2.Enable_1
  N3: Arduino2.D10_PWM/SS, IC2.Enable_2
  N4: Arduino2.D11_PWM/MOSI, U1.DS
  N5: Arduino2.D12/MISO, U1.ST_CP
  N6: Arduino2.D5_PWM, IC1.Enable_1
  N7: Arduino2.D6_PWM, IC1.Enable_2
  5V: Arduino2.5V, U1.MR, U1.VCC
  N8: Arduino2.GND, U1.OE
  N9: IC1.In_1, U1.Q0
  N10: IC1.Out_1_(_Controlled_by_Enable_1_), M1.pin_1
  N11: IC1.Out_2_(_Controlled_by_Enable_1_), M1.pin_2
  N12: IC1.In_2, U1.Q1
  N13: IC1.In_3, U1.Q3
  N14: IC1.Out_3_(_Controlled_by_Enable_2_), M4.pin_2
  N15: IC1.Out_4_(_Controlled_by_Enable_2_), M4.pin_1
  N16: IC1.In_4, U1.Q2
  N17: IC2.In_1, U1.Q4
  N18: IC2.Out_1_(_Controlled_by_Enable_1_), M2.pin_1
  N19: IC2.Out_2_(_Controlled_by_Enable_1_), M2.pin_2
  N20: IC2.In_2, U1.Q5
  N21: IC2.In_3, U1.Q7
  N22: IC2.Out_3_(_Controlled_by_Enable_2_), M3.pin_2
  N23: IC2.Out_4_(_Controlled_by_Enable_2_), M3.pin_1
  N24: IC2.In_4, U1.Q6

notes:
  This project shows how to control a DC motor's direction (running forwards and backwards) using an H-bridge. An H-bridge is an electronic circuit which enables a voltage to be applied across a load in either direction.
  http://itp.nyu.edu/physcomp/Labs/DCMotorControl
