# Fritzing sketch led_blink (saved by Fritzing 0.8.7b)
breadboards: 1

parts:
  元件1 = Arduino Uno (Rev3)
  LED1 = LED - 5mm [color="Red (633nm)" package="5 mm [THT]"]
  R1 = Resistor [tolerance=±5% resistance=100 package=THT]

nets:
  N1: 元件1.D10_PWM/SS, R1.Pin_1
  N2: 元件1.GND, LED1.cathode
  N3: LED1.anode, R1.Pin_0
