# Fritzing sketch circuit_layout (saved by Fritzing 0.8.7b)
breadboards: 1

parts:
  元件1 = Arduino Uno (Rev3)
  LED1 = LED - 5mm [color="Red (633nm)" package="5 mm [THT]"]
  R1 = Resistor [tolerance=±5% resistance=100 package=THT]
  LED2 = LED - 5mm [color="Red (633nm)" package="5 mm [THT]"]
  LED3 = LED - 5mm [color="Red (633nm)" package="5 mm [THT]"]
  R2 = Resistor [tolerance=±5% resistance=100 package=THT]
  R3 = Resistor [tolerance=±5% resistance=100 package=THT]

nets (from the breadboard view):
  N1: 元件1.D8, LED1.anode
  N2: 元件1.D9_PWM, LED2.anode
  N3: 元件1.D10_PWM/SS, LED3.anode
  N4: 元件1.GND, R1.Pin_0, R2.Pin_0, R3.Pin_0
  N5: LED1.cathode, R1.Pin_1
  N6: LED2.cathode, R3.Pin_1
  N7: LED3.cathode, R2.Pin_1
