# Fritzing sketch circuit_layout (saved by Fritzing 0.8.7b)
breadboards: 1

parts:
  元件1 = Arduino Uno (Rev3)
  LED1 = LED - 5mm [color="Red (633nm)" package="5 mm [THT]"]
  LED2 = LED - 5mm [color="Red (633nm)" package="5 mm [THT]"]
  LED3 = LED - 5mm [color="Red (633nm)" package="5 mm [THT]"]
  R2 = Resistor [tolerance=±5% resistance=220 package=THT]
  R3 = Resistor [tolerance=±5% resistance=220 package=THT]
  R4 = Resistor [tolerance=±5% resistance=220 package=THT]
  R5 = Resistor [tolerance=±5% resistance=220 package=THT]
  R6 = Resistor [tolerance=±5% resistance=1k package=THT]
  LED4 = LED - 5mm [color="Red (633nm)" package="5 mm [THT]"]
  LED5 = LED - 5mm [color="Red (633nm)" package="5 mm [THT]"]
  S1 = Pushbutton [package="[THT]"]
  R7 = Resistor [tolerance=±5% resistance=220 package=THT]

nets:
  N1: 元件1.D8, R7.Pin_1
  N2: 元件1.D9_PWM, R5.Pin_1
  N3: 元件1.D10_PWM/SS, LED3.anode, R2.Pin_0, R4.Pin_1
  N4: 元件1.D11_PWM/MOSI, R3.Pin_1
  N5: 元件1.D12/MISO, R2.Pin_1
  N6: 元件1.GND, LED1.cathode, LED2.cathode, LED3.cathode, R6.Pin_0, LED4.cathode, LED5.cathode, S1.Pin_1, S1.Pin_2
  N7: 元件1.D2, R6.Pin_1, S1.Pin_3, S1.Pin_4
  N8: LED1.anode, R4.Pin_0
  N9: LED2.anode, R3.Pin_0
  N10: R5.Pin_0, LED4.anode
  N11: LED5.anode, R7.Pin_0
