# Fritzing sketch circuit_layout (saved by Fritzing 0.8.7b)
breadboards: 1

parts:
  LED1 = LED - 5mm [color="Red (633nm)" package="5 mm [THT]"]
  LED2 = LED - 5mm [color="Red (633nm)" package="5 mm [THT]"]
  LED3 = LED - 5mm [color="Red (633nm)" package="5 mm [THT]"]
  R2 = Resistor [tolerance=±5% resistance=220 package=THT]
  LED4 = LED - 5mm [color="Red (633nm)" package="5 mm [THT]"]
  LED5 = LED - 5mm [color="Red (633nm)" package="5 mm [THT]"]
  LED6 = LED - 5mm [color="Red (633nm)" package="5 mm [THT]"]
  LED7 = LED - 5mm [color="Red (633nm)" package="5 mm [THT]"]
  LED8 = LED - 5mm [color="Red (633nm)" package="5 mm [THT]"]
  R3 = Resistor [tolerance=±5% resistance=220 package=THT]
  R4 = Resistor [tolerance=±5% resistance=220 package=THT]
  R5 = Resistor [tolerance=±5% resistance=220 package=THT]
  R6 = Resistor [tolerance=±5% resistance=220 package=THT]
  R7 = Resistor [tolerance=±5% resistance=220 package=THT]
  R8 = Resistor [tolerance=±5% resistance=220 package=THT]
  R9 = Resistor [tolerance=±5% resistance=220 package=THT]
  元件1 = Arduino Uno (Rev3)
  R10 = Rotary Potentiometer (Small) [maximum_resistance=100kΩ package=THT]

nets:
  N1: LED1.cathode, LED2.cathode, LED3.cathode, LED4.cathode, LED5.cathode, LED6.cathode, LED7.cathode, LED8.cathode, 元件1.GND, R10.leg2
  N2: LED1.anode, R4.Pin_0
  N3: LED2.anode, R3.Pin_0
  N4: LED3.anode, R2.Pin_0, R5.Pin_1, 元件1.D10_PWM/SS
  N5: R2.Pin_1, 元件1.D13/SCK
  N6: LED4.anode, R5.Pin_0
  N7: LED5.anode, R6.Pin_0
  N8: LED6.anode, R7.Pin_0
  N9: LED7.anode, R8.Pin_0
  N10: LED8.anode, R9.Pin_0
  N11: R3.Pin_1, 元件1.D12/MISO
  N12: R4.Pin_1, 元件1.D11_PWM/MOSI
  N13: R6.Pin_1, 元件1.D9_PWM
  N14: R7.Pin_1, 元件1.D8
  N15: R8.Pin_1, 元件1.D7
  N16: R9.Pin_1, 元件1.D6_PWM
  N17: 元件1.A2, R10.wiper
  N18: 元件1.5V, R10.leg1
