# Fritzing sketch circuit_layout (saved by Fritzing 0.8.7b)
breadboards: 1

parts:
  元件1 = Arduino Uno (Rev3)
  IC1 = L293D [package=THT]
  M1 = DC Motor

nets:
  N1: 元件1.D9_PWM, IC1.In_2
  N2: 元件1.D10_PWM/SS, IC1.In_1
  N3: 元件1.D11_PWM/MOSI, IC1.Enable_1
  N4: 元件1.3V3, IC1.+V
  N5: 元件1.5V, IC1.+Vmotor
  N6: 元件1.GND, IC1.0V
  N7: IC1.Out_1_(_Controlled_by_Enable_1_), M1.pin_2
  N8: IC1.Out_2_(_Controlled_by_Enable_1_), M1.pin_1
